# Fritzing sketch DHT 11 (saved by Fritzing 0.9.4)

parts:
  Part2 = Arduino Uno (Rev3) - ICSP
  R1 = Resistor [tolerance=±5% resistance=5.1k package=THT]
  DHT1 = DHT11 Humitidy and Temperature Sensor

nets:
  5V: Part2.5V, R1.Pin_0, DHT1.VDD
  GND: Part2.GND, DHT1.GND
  N1: R1.Pin_1, DHT1.DATA

custom parts:
  DHT11 Humitidy and Temperature Sensor: DHT11 Humidity and Temperature Sensor
