# Fritzing sketch DHT 22 (saved by Fritzing 0.9.4)

parts:
  Part2 = Arduino Uno (Rev3) - ICSP
  R1 = Resistor [tolerance=±5% resistance=5.1k package=THT]
  DHT22 = DHT22 Humidity and Temperature Sensor

nets:
  N1: Part2.D6_PWM, R1.Pin_1, DHT22.DATA
  5V: Part2.5V, R1.Pin_0, DHT22.VDD
  GND: Part2.GND, DHT22.GND
