# Fritzing sketch E18-D80NK Schematics (saved by Fritzing 0.9.4)

parts:
  IR_Sensor_Switch1 = Infrared Sensor Switch
  Part1 = Arduino Uno (Rev3) - ICSP

nets:
  N1: IR_Sensor_Switch1.OUT, Part1.D2
  GND: IR_Sensor_Switch1.GND, Part1.GND
  VCC: IR_Sensor_Switch1.Vcc, Part1.5V

notes:
  E18-D80NK
  Infrared Sensor

custom parts:
  Infrared Sensor Switch: - Working voltage: DC 5V - Working current: 10~15mA - Detecting range: 3~80cm (adjustable) - Red: VCC, Green: GND, Yellow: OUT
