# Fritzing sketch Voltage Divider Fritzing (saved by Fritzing 0.9.4)
breadboards: 1

parts:
  R1 = Resistor [tolerance=±5% resistance=9k package=THT]
  Part1 = Arduino Uno (Rev3) - ICSP
  R2 = Resistor [tolerance=±5% resistance=5k package=THT]
  BAT1 = BC9VPC [package=bc9vpc]

nets:
  N1: R1.Pin_0, Part1.A0, R2.Pin_1
  N2: R1.Pin_1, BAT1.V+
  N3: Part1.GND, R2.Pin_0, BAT1.V-
