# Fritzing sketch Output Digital Menggunakan LED (saved by Fritzing 0.9.3b)

parts:
  LED1 = LEDs [package=led10mm]
  Part1 = Arduino Uno (Rev3) - ICSP
  R1 = Resistor [tolerance=±5% resistance=220 package="0603 [SMD]"]

nets:
  N1: LED1.C, Part1.GND
  N2: LED1.A, R1.Pin_0
  N3: Part1.D7, R1.Pin_1
