# Fritzing sketch Input Digital Menggunakan Tombol (saved by Fritzing 0.9.3b)
breadboards: 1

parts:
  Part1 = Arduino Uno (Rev3) - ICSP
  Tombol_3 = Pushbutton [package="[SMD]"]
  Tombol_2 = Pushbutton [package="[SMD]"]
  Tombol_1 = Pushbutton [package="[SMD]"]
  R1 = Resistor [tolerance=±5% resistance=220 package="1206 [SMD]"]
  R2 = Resistor [tolerance=±5% resistance=220 package="1206 [SMD]"]

nets:
  N1: Part1.5V, Tombol_3.Pin_1, Tombol_3.Pin_2, R1.Pin_0
  N2: Part1.D8, Tombol_3.Pin_3, Tombol_3.Pin_4, R2.Pin_1
  N3: Part1.D4, Tombol_1.Pin_1, Tombol_1.Pin_2, R1.Pin_1
  N4: Part1.D6_PWM, Tombol_2.Pin_1, Tombol_2.Pin_2
  N5: Part1.GND, Tombol_2.Pin_3, Tombol_2.Pin_4, Tombol_1.Pin_3, Tombol_1.Pin_4, R2.Pin_0
