# Fritzing sketch Project Menyalakan LED Menggunakan Tombol (saved by Fritzing 0.9.3b)
breadboards: 1

parts:
  S1 = Pushbutton [package="[THT]"]
  R1 = Resistor [tolerance=±5% resistance=220 package=THT]
  LED1 = LED - 5mm [color="Red (633nm)" package="5 mm [THT]"]
  Part1 = Arduino Uno (Rev3) - ICSP

nets:
  N1: S1.Pin_1, S1.Pin_2, Part1.D2
  N2: S1.Pin_3, S1.Pin_4, LED1.cathode, Part1.GND
  N3: R1.Pin_0, LED1.anode
  N4: R1.Pin_1, Part1.D6_PWM
