# Fritzing sketch Schematic HC-05 Mega (saved by Fritzing 0.9.4)

parts:
  Part1 = Bluetooth HC-05 Macho
  Part2 = Arduino Mega ADK (Rev3)
  Part3 = Logic Level Converter

nets:
  N1: Part1.TXD, Part3.TX2_HV
  N2: Part1.RXD, Part3.RX2_HV
  VCC: Part1.VCC, Part2.5V, Part3.HV
  GND: Part1.GND, Part2.GND, Part3.GND
  N3: Part2.D19/RX1, Part3.TX2_LV
  N4: Part2.D18/TX1, Part3.RX2_LV
  N5: Part2.3V3, Part3.LV
