# Fritzing sketch Input Analog Menggunakan Potensio (saved by Fritzing 0.9.3b)

parts:
  Part1 = Arduino Uno (Rev3) - ICSP
  R3 = Rotary Potentiometer (Large) [maximum_resistance=100kΩ package=THT]

nets:
  N1: Part1.A0, R3.wiper
  N2: Part1.5V, R3.leg2
  N3: Part1.GND, R3.leg1
