# Fritzing sketch Mengatur Kecerahan LED dengan PWM (saved by Fritzing 0.9.3b)

parts:
  R1 = Resistor [tolerance=±5% resistance=220 package=THT]
  LED1 = LED - 5mm [color="Red (633nm)" package="5 mm [THT]"]
  Part1 = Arduino Uno (Rev3) - ICSP

nets:
  N1: R1.Pin_0, LED1.anode
  N2: R1.Pin_1, Part1.D6_PWM
  N3: LED1.cathode, Part1.GND
