# Fritzing sketch Project Mengatur Kecerahan LED Menggunakan Potensio (saved by Fritzing 0.9.3b)

parts:
  Part2 = Arduino Uno (Rev3) - ICSP
  R2 = Resistor [tolerance=±5% resistance=220 package=THT]
  LED2 = LED - 5mm [color="Red (633nm)" package="5 mm [THT]"]
  R4 = Rotary Potentiometer (Large) [maximum_resistance=100kΩ package=THT]
  R5 = Resistor [tolerance=±5% resistance=220 package=THT]
  LED3 = LED - 5mm [color="Red (633nm)" package="5 mm [THT]"]

nets:
  N1: Part2.A0, R4.wiper
  N2: Part2.GND, R4.leg1, LED3.cathode
  N3: Part2.D3_PWM, R2.Pin_1
  N4: Part2.D6_PWM, R5.Pin_1
  N5: Part2.5V, R4.leg2
  N6: R2.Pin_0, LED2.anode
  N7: R5.Pin_0, LED3.anode
