# Fritzing sketch GY 91 (saved by Fritzing 0.9.3b)

parts:
  MPU9250_MPU-1 = SparkFun IMU Breakout - MPU-9250 [part_number=" SEN-13762"]
  Part1 = Arduino Uno (Rev3) - ICSP

nets:
  N1: MPU9250_MPU-1.SCL/SCLK, Part1.A5/SCL
  N2: MPU9250_MPU-1.SDA/SDI, Part1.A4/SDA
  VDD: MPU9250_MPU-1.VDD, Part1.5V
  GND: MPU9250_MPU-1.GND, Part1.GND
