# Fritzing sketch MMA7361 (saved by Fritzing 0.9.3b)

parts:
  U1 = MMA7361 [package=lga14]
  Part1 = Arduino Uno (Rev3) - ICSP

nets:
  N1: U1.XOUT, Part1.A2
  N2: U1.YOUT, Part1.A1
  N3: U1.ZOUT, Part1.A0
  VSS: U1.VSS, Part1.GND
  VDD: U1.VDD, Part1.5V
  N4: U1.SLEEP, Part1.D5_PWM
  N5: U1.0GD, Part1.D4
  N6: U1.GSELECT, Part1.D3_PWM
  N7: U1.ST, Part1.D2

notes:
  MMA7361 <---> Arduino
  2(X Data) <---> A2
  3(Y Data) <---> A1
  4(Z Data) <---> A0
  5(Ground) <---> Ground
  6(Vin) <---> 5V
  7(Sleep) <---> 5
  9(Zero G) <---> 4
  10(G Select) <---> 3
  13(Self Test) <---> 2
