# Fritzing sketch Sensor Ultrasonik HC-SR04 (saved by Fritzing 0.9.3b)

parts:
  HC-SR04_Sensor_1 = HC-SR04 Ultrasonic Distance Sensor
  Part1 = Arduino Uno (Rev3) - ICSP

nets:
  VCC: HC-SR04_Sensor_1.VCC, Part1.5V
  N1: HC-SR04_Sensor_1.TRIG, Part1.D11_PWM/MOSI
  N2: HC-SR04_Sensor_1.ECHO, Part1.ICSP_MISO, Part1.D12/MISO
  GND: HC-SR04_Sensor_1.GND, Part1.GND
