# Fritzing sketch Output Suara Menggunakan Buzzer (saved by Fritzing 0.9.3b)

parts:
  Part1 = Arduino Uno (Rev3) - ICSP
  J1 = Piezo Speaker

nets:
  N1: Part1.D9_PWM, J1.pin2
  N2: Part1.GND, J1.pin1
