# Fritzing sketch Motor Vibration (saved by Fritzing 0.9.3b)

parts:
  Motor_Vibration = Vibration Motor- ROB-08449 [package=vibe-motor-10mm]  # not connected
  Part1 = Arduino Uno (Rev3) - ICSP
  2N2222 = NPN-Transistor [package="TO92 [THT]"]
  0_1uF = Ceramic Capacitor [capacitance="100 nF" package="0603 [SMD, multilayer]"]  # not connected
  1N4001 = Schottky Diode [part_number=1N5817 package="300 mil [THT]"]
  1K = Resistor [tolerance=±5% resistance=220 package="2512 [SMD]"]

nets:
  N1: Part1.D2, 1K.Pin_1
  N2: Part1.3V3, 1N4001.cathode
  N3: Part1.GND, 2N2222.C
  N4: 2N2222.E, 1N4001.anode
  N5: 2N2222.B, 1K.Pin_0
